# Fritzing sketch Steckplatine und Schaltplan (saved by Fritzing 1.0.5)
breadboards: 1

parts:
  Nana = Arduino Nano (Rev3.0)  # not connected
  zu_testender_IMU = InvenSense MPU6050
  Level_IMU = InvenSense MPU6050
  x/y-Achse = Stepper Motor - Bipolar  # not connected
  z-Achse = Stepper Motor - Bipolar
  DRV_1 = DRV 8825 Stepper Motor Carrier, High Current [part_number="DRV 8825"]
  DRV_2 = DRV 8825 Stepper Motor Carrier, High Current [part_number="DRV 8825"]  # not connected

nets:
  VCC: zu_testender_IMU.VCC, Level_IMU.VCC
  GND: zu_testender_IMU.GND, Level_IMU.GND
  N1: zu_testender_IMU.SCL, Level_IMU.SCL
  N2: zu_testender_IMU.SDA, Level_IMU.SDA
  N3: z-Achse.A, DRV_1.OUT_2B
  N4: z-Achse.C, DRV_1.OUT_2A
