# Fritzing sketch tests (saved by Fritzing 1.0.5)
breadboards: 1

parts:
  Nana = Arduino Nano (Rev3.0)
  z-Achse = Stepper Motor - Bipolar
  DRV_2 = DRV 8825 Stepper Motor Carrier, High Current [part_number="DRV 8825"]
  LED1 = LED - 5mm [color="Red (633nm)" current=0.030A package="5 mm [THT]"]
  R1 = Resistor [tolerance=±5% power=0.25W resistance=220 package=THT]

nets:
  N1: Nana.GND, LED1.cathode
  N2: Nana.D2, R1.Pin_0
  N3: z-Achse.A, DRV_2.OUT_2B
  N4: z-Achse.C, DRV_2.OUT_2A
  N5: z-Achse.B, DRV_2.OUT_1A
  N6: z-Achse.D, DRV_2.OUT_1B
  N7: LED1.anode, R1.Pin_1
