# Fritzing sketch wiring_diagramm (saved by Fritzing 1.0.5)
breadboards: 1

parts:
  Bauteil1 = Arduino Nano (Rev3.0)
  Power_plug1 = Power plug
  DRV_4 = DRV 8825 Stepper Motor Carrier, High Current [part_number="DRV 8825"]
  M1 = Stepper Motor - Bipolar  # not connected
  DRV_5 = DRV 8825 Stepper Motor Carrier, High Current [part_number="DRV 8825"]  # not connected
  C2 = Electrolytic Capacitor [capacitance=0.1mF voltage=35V mn=123 mpn=123 part_number=123 package="100 mil [THT, electrolytic]"]
  C3 = Electrolytic Capacitor [capacitance=0.1mF voltage=35V package="100 mil [THT, electrolytic]"]
  M2 = Stepper Motor - Bipolar  # not connected
  R1 = Resistor [tolerance=±5% power=0.25W resistance=10k package=THT]
  Level_IMU1 = InvenSense MPU6050

nets:
  GND: Bauteil1.GND, Power_plug1.GND, DRV_4.GROUND_LOG, C2.-, C3.-, Level_IMU1.GND
  VIN: Bauteil1.VIN, Power_plug1.VCC, C2.+, C3.+, R1.Pin_1
  5V: Bauteil1.5V, Level_IMU1.VCC
  N1: Bauteil1.A5, Level_IMU1.SCL
  N2: Bauteil1.A4, Level_IMU1.SDA

notes:
  C1 – 100µF 25V
  C2 – 100µF 25V
  J1 - 12V Power Supply
  U4 - IMU MPU6050
  M1/U1 - NEMA 17/DRV8825
  R1 - 10kΩ
  U3 - Arduino Nano
  M2/U2 - NEMA 17/DRV8825
