# Fritzing sketch wiring_diagramm_esp32 (saved by Fritzing 1.0.5)
breadboards: 3

parts:
  esp1 = ESP32 DevKitc V4
  Power_plug2 = Power plug
  C4 = Electrolytic Capacitor [capacitance=0.1mF voltage=35V package="100 mil [THT, electrolytic]"]
  M3 = Stepper Motor - Bipolar  # not connected
  Level_IMU2 = InvenSense MPU6050
  R2 = Resistor [tolerance=±5% power=0.25W resistance=10k package=THT]
  DRV_7 = DRV 8825 Stepper Motor Carrier, High Current [part_number="DRV 8825"]  # not connected
  DRV_8 = DRV 8825 Stepper Motor Carrier, High Current [part_number="DRV 8825"]  # not connected
  M4 = Stepper Motor - Bipolar  # not connected
  C5 = Electrolytic Capacitor [capacitance=0.1mF voltage=35V package="100 mil [THT, electrolytic]"]

nets:
  N1: esp1.IO21, Level_IMU2.SDA
  N2: esp1.IO22, Level_IMU2.SCL
  N3: esp1.GND#18, Level_IMU2.GND
  3V3: esp1.3V3, Level_IMU2.VCC, R2.Pin_1
  N4: Power_plug2.GND, C4.-, C5.-
  N5: Power_plug2.VCC, C4.+, C5.+

notes:
  C2 – 100µF 25V
  C1 – 100µF 25V
  J1 - 12V Power Supply
  U4 - IMU MPU6050
  R1 - 10kΩ
  M2/U2 - NEMA 17/DRV8825
  M1/U1 - NEMA 17/DRV8825
  U3 - ESP32 DEV KIT C

custom parts:
  ESP32 DevKitc V4: ESP32-DevKitC board with ESP32-WROOM-32 module. ESP32-DevKitC V4 is a small-sized ESP32-based development board produced by Espressif. Most of the pins on the ESP module are broken out to the pin headers on the board. The pins D0, D1, D2, D3, CMD and CLK are used internally for communication between ESP32 and SPI flash memory. They are grouped on both sides near the USB connector. Avoid using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
